// Digital circuit 27C1024.dig as structural Verilog
module _27C1024 (
  input  nCE,
  input  nOE,
  input  VPP,
  input  VDD,
  input  GND,
  input  I_O0,
  input  I_O1,
  input  I_O2,
  input  I_O3,
  input  I_O4,
  input  I_O5,
  input  I_O6,
  input  I_O7,
  input  A0,
  input  A1,
  input  A2,
  input  A3,
  input  A4,
  input  A5,
  input  A6,
  input  A7,
  input  A8,
  input  A9,
  input  A10,
  input  A11,
  input  A12,
  input  A13,
  input  A14,
  input  A15,
  input  I_O8,
  input  I_O9,
  input  I_O10,
  input  I_O11,
  input  I_O12,
  input  I_O13,
  input  I_O14,
  input  I_O15,
  input  VSS
);

  wire nor_1_out;
  wire [15:0] ROM1_d;

  PowerSupply powersupply_1 (.VDD(VDD), .GND(GND));
  EEPROM #(.AddrBits(16), .Bits(16)) ROM1 (
    .A({A15, A14, A13, A12, A11, A10, A9, A8, A7, A6, A5, A4, A3, A2, A1, A0}), .CS(~nCE), .WE(~VPP),
    .OE(~nOE), .D(ROM1_d));
  nor nor_1 (nor_1_out, nCE, ~VPP, nOE);  // NOr
  BusSplitter #(.Bits(16)) bussplitter_1 (
    .D(ROM1_d), .OE(nor_1_out), .D0(I_O0), .D1(I_O1), .D2(I_O2), .D3(I_O3), .D4(I_O4), .D5(I_O5), .D6(I_O6),
    .D7(I_O7), .D8(I_O8), .D9(I_O9), .D10(I_O10), .D11(I_O11), .D12(I_O12), .D13(I_O13), .D14(I_O14),
    .D15(I_O15));

  assign VSS = GND;

  // Notes on the sheet:
  //   nCE: pin 2, default 1
  //   nOE: pin 20, default 1
  //   VPP: pin 1, default 1
  //   VDD: pin 40, default 1
  //   GND: pin 11
  //   I_O0: pin 19
  //   I_O1: pin 18
  //   I_O2: pin 17
  //   I_O3: pin 16
  //   I_O4: pin 15
  //   I_O5: pin 14
  //   I_O6: pin 13
  //   I_O7: pin 12
  //   A0: pin 21
  //   A1: pin 22
  //   A2: pin 23
  //   A3: pin 24
  //   A4: pin 25
  //   A5: pin 26
  //   A6: pin 27
  //   A7: pin 28
  //   A8: pin 29
  //   A9: pin 31
  //   A10: pin 32
  //   A11: pin 33
  //   A12: pin 34
  //   A13: pin 35
  //   A14: pin 36
  //   A15: pin 37
  //   I_O8: pin 10
  //   I_O9: pin 9
  //   I_O10: pin 8
  //   I_O11: pin 7
  //   I_O12: pin 6
  //   I_O13: pin 5
  //   I_O14: pin 4
  //   I_O15: pin 3
  //   VSS: pin 30
  //   contents of ROM1 (hex, n*v repeats v):
  //   0,8018,c018,7cc1,100,1d6,ff00,69,ca,c2,69,bec,ff00,69,ca,61,14f0
  //   ,101,5fc,82,ff00,c2,16ec,1a0,1,15ec,1a0,100,8018,c018,0,18d2,19d6
  //   ,601,25f4,8d,bf60,6c2,701,2af4,681,c160,7c2,881,8c2,1801,180,21ec
  //   ,18d2,1901,180,21ec,19d6,300,8018,c018,ee00,16c2,290,100,17d6
  //   ,59dc,5edc,2bdc,22dc,b4dc,e2dc,dc,dc,fcdc,dc,200,5c2,ff00,ec2
  //   ,fc2,10c2,11c2,12c2,700,8018,c018,0,c2,2c2,2cc2,f00,8018,c018
  //   ,13c2,14c2,114,3e0,2ec2,4000,21c2,0,1cc2,114,f9ca,f6ca,f7ca,2cc2
  //   ,1ac2,200,1bc2,f600,ac2,bc2,cc2,ad00,22c2,e00,24c2,f900,25c2,1601
  //   ,2a0,16c2,314,e0,ea00,6*2,314,cbe0,f600,314,cbe0,f600,314,cbe0
  //   ,f600,314,cbe0,f600,314,cbe0,f600,314,cbe0,f600,314,cbe0,f600
  //   ,314,cbe0,f600,314,cbe0,f600,314,cbe0,f600,314,cbe0,f600,314,cbe0
  //   ,f600,314,cbe0,f600,314,cbe0,f600,314,cbe0,f600,1214,4be0,0,314
  //   ,cbe0,f600,314,cbe0,f600,314,cbe0,f600,314,cbe0,f600,314,cbe0
  //   ,f600,314,cbe0,f600,314,cbe0,f600,314,cbe0,f600,314,cbe0,f600
  //   ,314,cbe0,f600,314,cbe0,f600,314,cbe0,f600,314,cbe0,f600,314,cbe0
  //   ,f600,314,cbe0,f600,314,cbe0,f600,314,cbe0,f600,314,cbe0,f600
  //   ,314,cbe0,f600,314,cbe0,f600,1214,e9e0,1b15,fb14,d5e0,1901,2,2
  //   ,2419,2,314,cbe0,f500,18c3,0,19c2,2,314,cbe0,f400,515,ffe0,7f00
  //   ,c000,1fc2,8000,20c2,b300,9c2,100,80c2,e81,ec2,761,f61,681,6c2
  //   ,881,8c2,16e8,17fc,5360,6c60,781,7c2,2d01,1df0,1efc,1a0,2f01,2dc2
  //   ,22f0,23fc,0,100,2e81,27ec,28fc,e800,2ce4,2ec2,4880,fe,48fc,f00
  //   ,2ec2,48fc,1421,f00,700,300,100,200,400,800,400,200,100,300,700
  //   ,f00,e00,c00,800,400,200,100,200,400,800,c00,e00,14c2,1000,dc2
  //   ,e01,52f0,5500,1ec2,515,ffe0,2300,1214,e0,114,2101,fb20,21c2,2c01
  //   ,5cec,5dfc,0,f000,1441,14c2,2c01,63f0,64fc,1a0,0,2cc2,1f19,201
  //   ,2121,180,2019,2d6,7f00,fe29,fc89,feca,8030,5,ff89,fd89,ffca,fc20
  //   ,fb69,12,fa09,714,8d,7de8,7efc,3f20,3f00,381,3c2,1301,1214,1f19
  //   ,901,b1f4,280,9c2,bda0,8dec,da1,4000,92fc,1fc2,91ec,c000,93fc
  //   ,1fc2,1f01,2,4060,20c2,901,cf60,9aec,9bfc,fc3,c0,901,620,a6f0
  //   ,301,a400,1ec2,515,ffe0,3500,66fc,1f19,f40,1421,13c2,3c0,af00
  //   ,1ec2,515,ffe0,3300,66fc,1f19,2ee0,114,1101,ef60,beec,1201,1a0
  //   ,12c2,7f20,c6f0,ee00,c5fc,c4fc,100,bfec,1a0,2,8000,12c2,cbfc,2
  //   ,16c2,100,17c2,200,5c2,1101,df60,e2ec,b01,d5e8,a01,bc2,c01,ac2
  //   ,dafc,f600,a00,bc2,ac2,2,cc2,3500,dcec,1a0,2,11c2,eafc,0,201,320
  //   ,2c2,ea00,1ec2,515,ffe0,2600,114,f909,9c2,1fc2,f1ec,f2fc,100,ec00
  //   ,dc2,201,2121,180,214,b1e0,8018,6*2,aefc,201,ca00,dc2,114,911
  //   ,d,de,20c2,d,1f91,2015,c000,160*5d,c018,201,2121,180,8018,2d6
  //   ,7f00,fe29,fc89,feca,8030,5,ff89,fd89,ffca,fc20,fb69,12,fa09,714
  //   ,8d,c4e8,c5fc,3f20,3f00,381,3c2,1301,dfd,c018,d300,dc2,114,901
  //   ,190,1f01,8d,afd,1fd2,dc00,dc2,301,f40,1421,13c2,3c0,bfd,1f11,1f11
  //   ,901,eea0,e5f0,f080,9c2,100,cfd,dc2,3c0,e900,cfd,dc2,114,4e0,c000
  //   ,2001,8080,20d2,1f01,a5,f4f0,1fc2,f6fc,100,dc2,ff00,1ec2,515,ffe0
  //   ,3c00,4*2,3fc,1715,1581,be8,15c2,1601,280,16d2,d,de,fe,d,e80,ce4
  //   ,1a0,114,1ee1,0,18c2,de,d,19c2,1601,180,16c2,f600,1fc,12,5,414
  //   ,13e0,18c2,b14,bce0,12,180,1dc2,5,18c2,1d11,5,19c2,1fc,f600,12
  //   ,180,1dc2,1801,c6,1d11,1901,c6,1fc,f600,1901,40ec,1dc2,1801,43f0
  //   ,100,1dc2,d,fe,1d01,45ec,48f0,d,2,3dfc,d,1601,4afc,180,de,d,16c2
  //   ,1fc,f200,45f8,48e4,d,45f4,48e8,d,45e8,48f4,d,45e4,48f8,d,18c2
  //   ,0,19c2,fc,f800,12,1801,c6,fc,f800,1c11,5,1ac2,1c01,190,5,1bc2
  //   ,1c01,280,1cc2,1601,1a0,16c2,fc,f300,45f0,48ec,d,1c01,1b0,1b01
  //   ,c6,1c01,2a0,1cd2,1a01,6dfc,c6,1915,fbe0,1881,414,11e0,1821,b14
  //   ,b0e0,1601,1841,18c2,1fc,f900,1861,18c2,1fc,f900,16c2,fc,f900
  //   ,12,414,e4e0,100,b14,c8e0,12,180,1dc2,1801,85,18c2,a3e8,a5,a5fc
  //   ,45,25,2,8030,5,1981,1d11,85,19c2,1fc,f200,414,62e0,1601,2a0,16c2
  //   ,cbfc,f600,1581,afe8,2315,22e1,12,180,1dc2,1801,c1e8,a5,18c2,c4fc
  //   ,45,18c2,25,2,8030,1901,a5,1d11,a5,19c2,f200,1fc,1715,414,7e0
  //   ,1dc2,1601,280,1ac2,1701,1bc2,1d11,5,2a0,16c2,1d01,190,5,17d6
  //   ,1fc,f300,1c81,1cc2,1fc,f900,414,18e0,1dc2,414,26e0,1dc2,414,35e0
  //   ,1801,414,41e0,414,4ce0,414,57e0,1dc2,414,6de0,1dc2,414,7ae0,414
  //   ,86e0,414,91e0,414,9ce0,1dc2,1a01,2a0,16c2,1b01,17c2,314,cbe0
  //   ,f600,1601,280,18c2,1701,19c2,1d01,16c2,314,e0,f400,2,18c2,0,19c2
  //   ,314,cbe0,f500,1881,18c2,1ee8,1da1,20fc,1d41,1d21,2,8030,5,1981
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endmodule
