// Digital circuit gigatron.dig as structural Verilog
module gigatron (
  input  clk
);

  wire _74283_1_pin9, AC0, AC1, AC2, AC3, AC4, AC5, AC6, AC7, AL, ALU0, ALU1, ALU2, ALU3, ALU4, ALU5, ALU6,
       ALU7, and_1_out, AR0, AR1, AR2, AR3, BUS0, BUS1, BUS2, BUS3, BUS4, BUS5, BUS6, BUS7, CLK_t, CO,
       Condition_decoder_pin7, D0, D1, D2, D3, D4, D5, D6, D7, D_pin3, D_pin4, D_pin7, D_pin8, D_pin13,
       D_pin14, D_pin17, D_pin18, diodebackward_13_out, diodebackward_15_out, diodebackward_21_out, Down_out,
       EH, EL, Extended_Output_pin2, Extended_Output_pin5, Extended_Output_pin6, Extended_Output_pin9,
       Hardware_Breakpoint_eq, Input_Register_pin11, Input_Register_pin13, Input_Register_pin15,
       Input_Register_pin17, IR0, IR1, IR2, IR3, IR4, IR5, IR6, IR7, IR_pin3, IR_pin4, IR_pin7, IR_pin8,
       IR_pin13, IR_pin14, IR_pin17, IR_pin18, IX, jk_ff_1_nq, jk_ff_2_nq, Left_out, Logic_Unit_0_pin7,
       Logic_Unit_0_pin9, Logic_Unit_1_pin7, Logic_Unit_1_pin9, Logic_Unit_2_pin7, Logic_Unit_2_pin9,
       Logic_Unit_3_pin7, Logic_Unit_3_pin9, Logic_Unit_4_pin7, Logic_Unit_4_pin9, Logic_Unit_5_pin7,
       Logic_Unit_5_pin9, Logic_Unit_6_pin7, Logic_Unit_6_pin9, Logic_Unit_7_pin7, Logic_Unit_7_pin9,
       MAU0_pin4, MAU0_pin7, MAU0_pin9, MAU0_pin12, MAU1_pin4, MAU1_pin7, MAU1_pin9, MAU1_pin12, MAU2_pin4,
       MAU2_pin7, MAU2_pin9, MAU2_pin12, MAU3_pin4, MAU3_pin9, MAU3_pin12, Mode_decoder_pin6,
       Mode_decoder_pin7, Mode_decoder_pin9, Mode_decoder_pin12, Mode_decoder_pin13, Mode_decoder_pin14,
       Mode_decoder_pin15, nAE, nBF, nDE, nIE, nLD, nOE, nOL, not_1_out, not_3_out, not_4_out, nPH, nPL, nWE,
       nXL, nYL, Operation_decoder_pin9, Operation_decoder_pin10, Operation_decoder_pin11,
       Operation_decoder_pin12, Operation_decoder_pin13, Operation_decoder_pin14, Operation_decoder_pin15,
       OUT0, OUT1, OUT2, OUT3, OUT4, OUT5, OUT6, OUT7, PC0, PC1, PC2, PC3, PC4, PC5, PC6, PC7, PC8, PC9,
       PC10, PC11, PC12, PC13, PC14, PC15, PC_0_3_pin15, PC_8_11_pin10, PC_12_15_pin10, PIXCLK, pullup_1_out,
       pullup_2_out, pullup_7_out, pullup_8_out, Right_out, RST, switch_1_b, switch_3_b, Up_out, X0, X1, X2,
       X3, X4, X5, X6, X7, X_register_H_pin10, Y0, Y1, Y2, Y3, Y4, Y5, Y6, Y7;

  DipSwitch #(.dipDefault("true")) Right (.out(Right_out));
  DipSwitch #(.dipDefault("true")) Left (.out(Left_out));
  DipSwitch #(.dipDefault("true")) Down (.out(Down_out));
  DipSwitch #(.dipDefault("true")) Up (.out(Up_out));
  Seven_Seg_Hex seven_seg_hex_1 (.d({PC15, PC14, PC13, PC12}), .dp(1'b0));
  Seven_Seg_Hex seven_seg_hex_2 (.d({AC7, AC6, AC5, AC4}), .dp(1'b0));
  _74244 Input_Register (
    .pin1(nIE), .pin2(Right_out), .pin3(BUS7), .pin4(Left_out), .pin5(BUS6), .pin6(Down_out), .pin7(BUS5),
    .pin8(Up_out), .pin9(BUS4), .pin10(1'b0), .pin11(Input_Register_pin11), .pin12(BUS3),
    .pin13(Input_Register_pin13), .pin14(BUS2), .pin15(Input_Register_pin15), .pin16(BUS1),
    .pin17(Input_Register_pin17), .pin18(BUS0), .pin19(nIE), .pin20(1'b1));
  Seven_Seg_Hex seven_seg_hex_3 (.d({PC11, PC10, PC9, PC8}), .dp(1'b0));
  Seven_Seg_Hex seven_seg_hex_4 (.d({AC3, AC2, AC1, AC0}), .dp(1'b0));
  _74161 X_register_H (
    .pin1(1'b1), .pin2(CLK_t), .pin3(ALU4), .pin4(ALU5), .pin5(ALU6), .pin6(ALU7), .pin7(IX), .pin8(1'b0),
    .pin9(nXL), .pin10(X_register_H_pin10), .pin11(X7), .pin12(X6), .pin13(X5), .pin14(X4), .pin16(1'b1));  // open: pin15
  _74161 X_register_L (
    .pin1(1'b1), .pin2(CLK_t), .pin3(ALU0), .pin4(ALU1), .pin5(ALU2), .pin6(ALU3), .pin7(IX), .pin8(1'b0),
    .pin9(nXL), .pin10(1'b1), .pin11(X3), .pin12(X2), .pin13(X1), .pin14(X0), .pin15(X_register_H_pin10),
    .pin16(1'b1));
  _74244 Bus_gateway_AC (
    .pin1(nAE), .pin2(AC0), .pin3(BUS4), .pin4(AC1), .pin5(BUS5), .pin6(AC2), .pin7(BUS6), .pin8(AC3),
    .pin9(BUS7), .pin10(1'b0), .pin11(AC7), .pin12(BUS3), .pin13(AC6), .pin14(BUS2), .pin15(AC5),
    .pin16(BUS1), .pin17(AC4), .pin18(BUS0), .pin19(nAE), .pin20(1'b1));
  Seven_Seg_Hex seven_seg_hex_5 (.d({PC7, PC6, PC5, PC4}), .dp(1'b0));
  Seven_Seg_Hex seven_seg_hex_6 (.d({PC3, PC2, PC1, PC0}), .dp(1'b0));
  Seven_Seg_Hex seven_seg_hex_7 (.d({X7, X6, X5, X4}), .dp(1'b0));
  Seven_Seg_Hex seven_seg_hex_8 (.d({X3, X2, X1, X0}), .dp(1'b0));
  DipSwitch #(.dipDefault("true")) A (.out(Input_Register_pin17));
  DipSwitch #(.dipDefault("true")) B (.out(Input_Register_pin15));
  DipSwitch #(.dipDefault("true")) Select (.out(Input_Register_pin13));
  DipSwitch #(.dipDefault("true")) Start (.out(Input_Register_pin11));
  Seven_Seg_Hex seven_seg_hex_9 (.d({IR7, IR6, IR5, IR4}), .dp(1'b0));
  Seven_Seg_Hex seven_seg_hex_10 (.d({IR3, IR2, IR1, IR0}), .dp(1'b0));
  Seven_Seg_Hex seven_seg_hex_11 (.d({Y7, Y6, Y5, Y4}), .dp(1'b0));
  _74377 Accumulator (
    .pin1(nLD), .pin2(AC3), .pin3(ALU3), .pin4(ALU2), .pin5(AC2), .pin6(AC1), .pin7(ALU1), .pin8(ALU0),
    .pin9(AC0), .pin10(1'b0), .pin11(CLK_t), .pin12(AC5), .pin13(ALU5), .pin14(ALU4), .pin15(AC4),
    .pin16(AC7), .pin17(ALU7), .pin18(ALU6), .pin19(AC6), .pin20(1'b1));
  _74377 Y_register (
    .pin1(nYL), .pin2(Y0), .pin3(ALU0), .pin4(ALU1), .pin5(Y1), .pin6(Y2), .pin7(ALU2), .pin8(ALU3),
    .pin9(Y3), .pin10(1'b0), .pin11(CLK_t), .pin12(Y7), .pin13(ALU7), .pin14(ALU6), .pin15(Y6), .pin16(Y5),
    .pin17(ALU5), .pin18(ALU4), .pin19(Y4), .pin20(1'b1));
  _74377 Output_register (
    .pin1(nOL), .pin2(OUT3), .pin3(ALU3), .pin4(ALU2), .pin5(OUT2), .pin6(OUT1), .pin7(ALU1), .pin8(ALU0),
    .pin9(OUT0), .pin10(1'b0), .pin11(CLK_t), .pin12(OUT4), .pin13(ALU4), .pin14(ALU5), .pin15(OUT5),
    .pin16(OUT6), .pin17(ALU6), .pin18(ALU7), .pin19(OUT7), .pin20(1'b1));
  Seven_Seg_Hex seven_seg_hex_12 (.d({Y3, Y2, Y1, Y0}), .dp(1'b0));
  Seven_Seg_Hex seven_seg_hex_13 (.d({OUT7, OUT6, OUT5, OUT4}), .dp(1'b0));
  Seven_Seg_Hex seven_seg_hex_14 (.d({D7, D6, D5, D4}), .dp(1'b0));
  Comparator #(.Bits(16)) Hardware_Breakpoint (
    .a({PC15, PC14, PC13, PC12, PC11, PC10, PC9, PC8, PC7, PC6, PC5, PC4, PC3, PC2, PC1, PC0}), .b(16'h8000),
    .eq(Hardware_Breakpoint_eq));  // open: gt, lt
  Seven_Seg_Hex seven_seg_hex_15 (.d({OUT3, OUT2, OUT1, OUT0}), .dp(1'b0));
  Seven_Seg_Hex seven_seg_hex_16 (.d({D3, D2, D1, D0}), .dp(1'b0));
  not not_1 (not_1_out, Hardware_Breakpoint_eq);
  Switch #(.Closed("true")) switch_1 (.A(clk), .B(switch_1_b));
  JK_FF jk_ff_1 (.J(1'b1), .C(PIXCLK), .K(1'b1), .nQ(jk_ff_1_nq));  // open: Q
  and and_1 (and_1_out, not_1_out, switch_1_b);
  Reset reset_1 (.out(RST));
  JK_FF jk_ff_2 (.J(1'b1), .C(jk_ff_1_nq), .K(1'b1), .nQ(jk_ff_2_nq));  // open: Q
  Seven_Seg_Hex seven_seg_hex_17 (.d({BUS7, BUS6, BUS5, BUS4}), .dp(1'b0));
  Seven_Seg_Hex seven_seg_hex_18 (.d({BUS3, BUS2, BUS1, BUS0}), .dp(1'b0));
  Switch #(.Closed("true")) switch_2 (.A(and_1_out), .B(PIXCLK));
  Switch switch_3 (.A(PIXCLK), .B(switch_3_b));
  Button button_1 (.out(switch_3_b));
  Switch #(.Closed("true")) switch_4 (.A(jk_ff_2_nq), .B(CLK_t));
  _74157 MAU0 (
    .pin1(EL), .pin2(X4), .pin3(D4), .pin4(MAU0_pin4), .pin5(X5), .pin6(D5), .pin7(MAU0_pin7), .pin8(1'b0),
    .pin9(MAU0_pin9), .pin10(D6), .pin11(X6), .pin12(MAU0_pin12), .pin13(D7), .pin14(X7), .pin15(1'b0),
    .pin16(1'b1));
  _74157 MAU1 (
    .pin1(EL), .pin2(X1), .pin3(D1), .pin4(MAU1_pin4), .pin5(X2), .pin6(D2), .pin7(MAU1_pin7), .pin8(1'b0),
    .pin9(MAU1_pin9), .pin10(D3), .pin11(X3), .pin12(MAU1_pin12), .pin13(D0), .pin14(X0), .pin15(1'b0),
    .pin16(1'b1));
  _74157 MAU2 (
    .pin1(1'b0), .pin2(Y5), .pin3(1'b1), .pin4(MAU2_pin4), .pin5(Y6), .pin6(1'b1), .pin7(MAU2_pin7),
    .pin8(1'b0), .pin9(MAU2_pin9), .pin10(1'b1), .pin11(Y3), .pin12(MAU2_pin12), .pin13(1'b1), .pin14(Y1),
    .pin15(EH), .pin16(1'b1));
  _74157 MAU3 (
    .pin1(1'b0), .pin2(Y0), .pin3(1'b1), .pin4(MAU3_pin4), .pin5(Y7), .pin6(1'b1), .pin8(1'b0),
    .pin9(MAU3_pin9), .pin10(1'b1), .pin11(Y2), .pin12(MAU3_pin12), .pin13(1'b1), .pin14(Y4), .pin15(EH),
    .pin16(1'b1));  // open: pin7
  LED led_1 (.in(Extended_Output_pin2));
  LED led_2 (.in(Extended_Output_pin5));
  VGA VGA (.R({OUT1, OUT0}), .G({OUT3, OUT2}), .B({OUT5, OUT4}), .H(OUT6), .V(OUT7), .C(PIXCLK));
  LED led_3 (.in(Extended_Output_pin6));
  _74244 D_Buffer (
    .pin1(nDE), .pin2(D6), .pin3(BUS4), .pin4(D7), .pin5(BUS2), .pin6(D5), .pin7(BUS0), .pin8(D3),
    .pin9(BUS1), .pin10(1'b0), .pin11(D1), .pin12(BUS3), .pin13(D0), .pin14(BUS5), .pin15(D2), .pin16(BUS7),
    .pin17(D4), .pin18(BUS6), .pin19(nDE), .pin20(1'b1));
  LED led_4 (.in(Extended_Output_pin9));
  _74273 Extended_Output (
    .pin1(1'b1), .pin2(Extended_Output_pin2), .pin3(AC3), .pin4(AC2), .pin5(Extended_Output_pin5),
    .pin6(Extended_Output_pin6), .pin7(AC1), .pin8(AC0), .pin9(Extended_Output_pin9), .pin10(1'b0),
    .pin11(OUT6), .pin13(AC4), .pin14(AC5), .pin17(AC6), .pin18(AC7), .pin20(1'b1));  // open: pin12, pin15, pin16, pin19
  _74273 D (
    .pin1(1'b1), .pin2(D0), .pin3(D_pin3), .pin4(D_pin4), .pin5(D1), .pin6(D2), .pin7(D_pin7), .pin8(D_pin8),
    .pin9(D3), .pin10(1'b0), .pin11(CLK_t), .pin12(D4), .pin13(D_pin13), .pin14(D_pin14), .pin15(D5),
    .pin16(D6), .pin17(D_pin17), .pin18(D_pin18), .pin19(D7), .pin20(1'b1));
  _74273 IR (
    .pin1(1'b1), .pin2(IR0), .pin3(IR_pin3), .pin4(IR_pin4), .pin5(IR1), .pin6(IR2), .pin7(IR_pin7),
    .pin8(IR_pin8), .pin9(IR3), .pin10(1'b0), .pin11(CLK_t), .pin12(IR4), .pin13(IR_pin13), .pin14(IR_pin14),
    .pin15(IR5), .pin16(IR6), .pin17(IR_pin17), .pin18(IR_pin18), .pin19(IR7), .pin20(1'b1));
  // CustomRam customram_1: pin names not known; wires that end beside it: 1'b0, BUS2, BUS1, BUS0, MAU1_pin12, BUS7, MAU1_pin4, 1'b0, MAU1_pin7, MAU3_pin9, MAU1_pin9, nOE, MAU0_pin4, MAU2_pin9, MAU0_pin7, MAU2_pin12, MAU0_pin9, MAU3_pin4, MAU0_pin12, MAU2_pin4, MAU3_pin12, nWE, MAU2_pin7, 1'b1
  _74153 Logic_Unit_3 (
    .pin1(1'b0), .pin2(BUS3), .pin3(AR3), .pin4(AR2), .pin5(AR1), .pin6(AR0), .pin7(Logic_Unit_3_pin7),
    .pin8(1'b0), .pin9(Logic_Unit_3_pin9), .pin10(1'b0), .pin11(1'b1), .pin12(1'b0), .pin13(1'b1),
    .pin14(AC3), .pin15(AL), .pin16(1'b1));
  _74153 Logic_Unit_7 (
    .pin1(AL), .pin2(BUS7), .pin3(1'b1), .pin4(1'b0), .pin5(1'b1), .pin6(1'b0), .pin7(Logic_Unit_7_pin7),
    .pin8(1'b0), .pin9(Logic_Unit_7_pin9), .pin10(AR0), .pin11(AR1), .pin12(AR2), .pin13(AR3), .pin14(AC7),
    .pin15(1'b0), .pin16(1'b1));
  _27C1024 ROM (
    .nCE(1'b0), .nOE(1'b0), .VPP(1'b1), .VDD(1'b1), .GND(1'b0), .I_O0(IR_pin3), .I_O1(IR_pin4),
    .I_O2(IR_pin7), .I_O3(IR_pin8), .I_O4(IR_pin13), .I_O5(IR_pin14), .I_O6(IR_pin17), .I_O7(IR_pin18),
    .A0(PC0), .A1(PC1), .A2(PC2), .A3(PC3), .A4(PC4), .A5(PC5), .A6(PC6), .A7(PC7), .A8(PC8), .A9(PC9),
    .A10(PC10), .A11(PC11), .A12(PC12), .A13(PC13), .A14(PC14), .A15(PC15), .I_O8(D_pin3), .I_O9(D_pin4),
    .I_O10(D_pin7), .I_O11(D_pin8), .I_O12(D_pin13), .I_O13(D_pin14), .I_O14(D_pin17), .I_O15(D_pin18),
    .VSS(1'b0));
  _74161 PC_0_3 (
    .pin1(RST), .pin2(CLK_t), .pin3(BUS0), .pin4(BUS1), .pin5(BUS2), .pin6(BUS3), .pin7(1'b1), .pin8(1'b0),
    .pin9(nPL), .pin10(1'b1), .pin11(PC3), .pin12(PC2), .pin13(PC1), .pin14(PC0), .pin15(PC_0_3_pin15),
    .pin16(1'b1));
  _74153 Logic_Unit_2 (
    .pin1(1'b0), .pin2(BUS2), .pin3(AR3), .pin4(AR2), .pin5(AR1), .pin6(AR0), .pin7(Logic_Unit_2_pin7),
    .pin8(1'b0), .pin9(Logic_Unit_2_pin9), .pin10(1'b0), .pin11(1'b1), .pin12(1'b0), .pin13(1'b1),
    .pin14(AC2), .pin15(AL), .pin16(1'b1));
  _74153 Logic_Unit_6 (
    .pin1(AL), .pin2(BUS6), .pin3(1'b1), .pin4(1'b0), .pin5(1'b1), .pin6(1'b0), .pin7(Logic_Unit_6_pin7),
    .pin8(1'b0), .pin9(Logic_Unit_6_pin9), .pin10(AR0), .pin11(AR1), .pin12(AR2), .pin13(AR3), .pin14(AC6),
    .pin15(1'b0), .pin16(1'b1));
  _74161 PC_12_15 (
    .pin1(RST), .pin2(CLK_t), .pin3(Y4), .pin4(Y5), .pin5(Y6), .pin6(Y7), .pin7(1'b1), .pin8(1'b0),
    .pin9(nPH), .pin10(PC_12_15_pin10), .pin11(PC15), .pin12(PC14), .pin13(PC13), .pin14(PC12), .pin16(1'b1));  // open: pin15
  _74161 PC_8_11 (
    .pin1(RST), .pin2(CLK_t), .pin3(Y0), .pin4(Y1), .pin5(Y2), .pin6(Y3), .pin7(1'b1), .pin8(1'b0),
    .pin9(nPH), .pin10(PC_8_11_pin10), .pin11(PC11), .pin12(PC10), .pin13(PC9), .pin14(PC8),
    .pin15(PC_12_15_pin10), .pin16(1'b1));
  _74161 PC_4_7 (
    .pin1(RST), .pin2(CLK_t), .pin3(BUS4), .pin4(BUS5), .pin5(BUS6), .pin6(BUS7), .pin7(1'b1), .pin8(1'b0),
    .pin9(nPL), .pin10(PC_0_3_pin15), .pin11(PC7), .pin12(PC6), .pin13(PC5), .pin14(PC4),
    .pin15(PC_8_11_pin10), .pin16(1'b1));
  _74153 Logic_Unit_1 (
    .pin1(1'b0), .pin2(BUS1), .pin3(AR3), .pin4(AR2), .pin5(AR1), .pin6(AR0), .pin7(Logic_Unit_1_pin7),
    .pin8(1'b0), .pin9(Logic_Unit_1_pin9), .pin10(1'b0), .pin11(1'b1), .pin12(1'b0), .pin13(1'b1),
    .pin14(AC1), .pin15(AL), .pin16(1'b1));
  _74153 Logic_Unit_5 (
    .pin1(AL), .pin2(BUS5), .pin3(1'b1), .pin4(1'b0), .pin5(1'b1), .pin6(1'b0), .pin7(Logic_Unit_5_pin7),
    .pin8(1'b0), .pin9(Logic_Unit_5_pin9), .pin10(AR0), .pin11(AR1), .pin12(AR2), .pin13(AR3), .pin14(AC5),
    .pin15(1'b0), .pin16(1'b1));
  _74153 Logic_Unit_0 (
    .pin1(1'b0), .pin2(BUS0), .pin3(AR3), .pin4(AR2), .pin5(AR1), .pin6(AR0), .pin7(Logic_Unit_0_pin7),
    .pin8(1'b0), .pin9(Logic_Unit_0_pin9), .pin10(1'b0), .pin11(1'b1), .pin12(1'b0), .pin13(1'b1),
    .pin14(AC0), .pin15(AL), .pin16(1'b1));
  _74153 Logic_Unit_4 (
    .pin1(AL), .pin2(BUS4), .pin3(1'b1), .pin4(1'b0), .pin5(1'b1), .pin6(1'b0), .pin7(Logic_Unit_4_pin7),
    .pin8(1'b0), .pin9(Logic_Unit_4_pin9), .pin10(AR0), .pin11(AR1), .pin12(AR2), .pin13(AR3), .pin14(AC4),
    .pin15(1'b0), .pin16(1'b1));
  _74139 Jump_detector___Bus_access_decoder (
    .pin1(1'b0), .pin2(IR0), .pin3(IR1), .pin4(nDE), .pin5(nOE), .pin6(nAE), .pin7(nIE), .pin8(1'b0),
    .pin12(nBF), .pin13(IR2), .pin14(IR3), .pin15(IR4), .pin16(1'b1));  // open: pin9, pin10, pin11
  _74138 Mode_decoder (
    .pin1(IR2), .pin2(IR3), .pin3(IR4), .pin4(1'b0), .pin5(1'b0), .pin6(Mode_decoder_pin6),
    .pin7(Mode_decoder_pin7), .pin8(1'b0), .pin9(Mode_decoder_pin9), .pin10(nYL), .pin11(nXL),
    .pin12(Mode_decoder_pin12), .pin13(Mode_decoder_pin13), .pin14(Mode_decoder_pin14),
    .pin15(Mode_decoder_pin15), .pin16(1'b1));
  PullUp pullup_1 (.out(pullup_1_out));
  DiodeBackward diodebackward_1 (.in(Mode_decoder_pin15), .out(pullup_1_out));
  DiodeBackward diodebackward_2 (.in(Mode_decoder_pin14), .out(pullup_1_out));
  DiodeBackward diodebackward_3 (.in(Mode_decoder_pin13), .out(pullup_1_out));
  DiodeBackward diodebackward_4 (.in(Mode_decoder_pin12), .out(pullup_1_out));
  not not_2 (IX, Mode_decoder_pin7);
  not not_3 (not_3_out, Operation_decoder_pin9);
  PullUp pullup_2 (.out(pullup_2_out));
  DiodeBackward diodebackward_5 (.in(Mode_decoder_pin14), .out(EL));
  DiodeBackward diodebackward_6 (.in(Mode_decoder_pin12), .out(EL));
  DiodeBackward diodebackward_7 (.in(Mode_decoder_pin9), .out(pullup_2_out));
  DiodeBackward diodebackward_8 (.in(Mode_decoder_pin7), .out(EL));
  DiodeBackward diodebackward_9 (.in(Mode_decoder_pin7), .out(pullup_2_out));
  or or_1 (nLD, pullup_1_out, not_3_out);
  PullUp pullup_3 (.out(EL));
  DiodeBackward diodebackward_10 (.in(Mode_decoder_pin13), .out(EH));
  DiodeBackward diodebackward_11 (.in(Mode_decoder_pin12), .out(EH));
  DiodeBackward diodebackward_12 (.in(Mode_decoder_pin7), .out(EH));
  or or_2 (nOL, pullup_2_out, not_3_out);
  PullUp pullup_4 (.out(EH));
  _74283 _74283_1 (
    .pin1(ALU1), .pin2(Logic_Unit_1_pin9), .pin3(Logic_Unit_1_pin7), .pin4(ALU0), .pin5(Logic_Unit_0_pin7),
    .pin6(Logic_Unit_0_pin9), .pin7(AR0), .pin8(1'b0), .pin9(_74283_1_pin9), .pin10(ALU3),
    .pin11(Logic_Unit_3_pin9), .pin12(Logic_Unit_3_pin7), .pin13(ALU2), .pin14(Logic_Unit_2_pin7),
    .pin15(Logic_Unit_2_pin9), .pin16(1'b1));
  _74283 _74283_2 (
    .pin1(ALU5), .pin2(Logic_Unit_5_pin7), .pin3(Logic_Unit_5_pin9), .pin4(ALU4), .pin5(Logic_Unit_4_pin7),
    .pin6(Logic_Unit_4_pin9), .pin7(_74283_1_pin9), .pin8(1'b0), .pin9(CO), .pin10(ALU7),
    .pin11(Logic_Unit_7_pin9), .pin12(Logic_Unit_7_pin7), .pin13(ALU6), .pin14(Logic_Unit_6_pin9),
    .pin15(Logic_Unit_6_pin7), .pin16(1'b1));
  _74138 Operation_decoder (
    .pin1(IR5), .pin2(IR6), .pin3(IR7), .pin4(1'b0), .pin5(1'b0), .pin6(1'b1), .pin7(Mode_decoder_pin6),
    .pin8(1'b0), .pin9(Operation_decoder_pin9), .pin10(Operation_decoder_pin10),
    .pin11(Operation_decoder_pin11), .pin12(Operation_decoder_pin12), .pin13(Operation_decoder_pin13),
    .pin14(Operation_decoder_pin14), .pin15(Operation_decoder_pin15), .pin16(1'b1));
  DiodeBackward diodebackward_13 (.in(IR7), .out(diodebackward_13_out));
  DiodeBackward diodebackward_14 (.in(Mode_decoder_pin6), .out(diodebackward_13_out));
  or or_3 (nWE, Operation_decoder_pin9, CLK_t);
  PullUp pullup_5 (.out(diodebackward_13_out));
  DiodeBackward diodebackward_15 (.in(Operation_decoder_pin10), .out(diodebackward_15_out));
  DiodeBackward diodebackward_16 (.in(Mode_decoder_pin6), .out(diodebackward_15_out));
  PullUp pullup_6 (.out(diodebackward_15_out));
  PullUp pullup_7 (.out(pullup_7_out));
  DiodeBackward diodebackward_17 (.in(Operation_decoder_pin13), .out(pullup_7_out));
  DiodeBackward diodebackward_18 (.in(Operation_decoder_pin12), .out(pullup_7_out));
  DiodeBackward diodebackward_19 (.in(Operation_decoder_pin10), .out(pullup_7_out));
  PullUp pullup_8 (.out(pullup_8_out));
  DiodeBackward diodebackward_20 (.in(Operation_decoder_pin15), .out(pullup_8_out));
  DiodeBackward diodebackward_21 (.in(Operation_decoder_pin15), .out(diodebackward_21_out));
  DiodeBackward diodebackward_22 (.in(Operation_decoder_pin14), .out(diodebackward_21_out));
  DiodeBackward diodebackward_23 (.in(Operation_decoder_pin13), .out(diodebackward_21_out));
  DiodeBackward diodebackward_24 (.in(Operation_decoder_pin13), .out(pullup_8_out));
  DiodeBackward diodebackward_25 (.in(Operation_decoder_pin12), .out(pullup_8_out));
  DiodeBackward diodebackward_26 (.in(Operation_decoder_pin11), .out(diodebackward_21_out));
  DiodeBackward diodebackward_27 (.in(Operation_decoder_pin11), .out(pullup_8_out));
  DiodeBackward diodebackward_28 (.in(Mode_decoder_pin6), .out(pullup_8_out));
  PullUp pullup_9 (.out(diodebackward_21_out));
  or or_4 (nPH, Mode_decoder_pin6, nBF);
  _74540 _74540_1 (
    .pin1(1'b0), .pin2(diodebackward_21_out), .pin3(pullup_8_out), .pin4(pullup_7_out),
    .pin5(diodebackward_15_out), .pin6(diodebackward_13_out), .pin7(1'b0), .pin8(1'b0), .pin9(1'b0),
    .pin10(1'b0), .pin14(AL), .pin15(AR0), .pin16(AR1), .pin17(AR2), .pin18(AR3), .pin19(1'b0), .pin20(1'b1));  // open: pin11, pin12, pin13
  not not_4 (not_4_out, Condition_decoder_pin7);
  DiodeBackward diodebackward_29 (.in(not_4_out), .out(nPL));
  DiodeBackward diodebackward_30 (.in(nPH), .out(nPL));
  _74153 Condition_decoder (
    .pin1(Mode_decoder_pin6), .pin2(CO), .pin3(1'b0), .pin4(IR4), .pin5(IR3), .pin6(IR2),
    .pin7(Condition_decoder_pin7), .pin8(1'b0), .pin10(1'b1), .pin11(1'b1), .pin12(1'b1), .pin13(1'b1),
    .pin14(AC7), .pin15(1'b1), .pin16(1'b1));  // open: pin9
  PullUp pullup_10 (.out(nPL));

  // Notes on the sheet:
  //   clk: Hz: 25175000
  //   Program Counter
  //   Accumulator
  //   X Register
  //   Instruction
  //   Y Register
  //   Output
  //   Data
  //   Bus Data
  //   JUMP
  //   STORE
  //   LOAD
  //   AND
  //   OR
  //   XOR
  //   ADD
  //   SUB
endmodule
