// Logisim project Gigatron.circ as structural Verilog: 1 circuit, main circuit 74377 Register
module _74377_Register (
  input  CLK,
  input  CLK_2,
  input  nE1,
  input  _1C0,
  input  nCLR,
  input  nENABLE,
  input  _1C1,
  input  D0,
  input  D0_2,
  input  _1C2,
  input  _1C3,
  input  B,
  input  A,
  input  _2C0,
  input  D1,
  input  D1_2,
  input  _2C1,
  input  _2C2,
  input  _2C3,
  input  D2,
  input  nE2,
  input  D2_2,
  input  D3,
  input  CLK_3,
  input  D3_2,
  input  nCLR_2,
  input  CLK_4,
  input  D4,
  input  D,
  input  D_2,
  input  D4_2,
  input  D5,
  input  CLK_5,
  input  nCLR_3,
  input  D5_2,
  input  nLOAD,
  input  D6,
  input  ENP,
  input  ENT,
  input  D6_2,
  input  DATA_A,
  input  D7,
  input  D7_2,
  input  DATA_B,
  input  DATA_C,
  input  DATA_C_2,
  output Q0,
  output Q0_2,
  output Q1,
  output Q1_2,
  output Q2,
  output Q2_2,
  output Q3,
  output Q3_2,
  output Q4,
  output Q,
  output QA,
  output Q4_2,
  output Q5,
  output Q5_2,
  output Q6,
  output QA_2,
  output Q6_2,
  output Q7,
  output QB,
  output Q7_2,
  output QC,
  output QD,
  output RCO
);

  wire and_1_out, and_2_out, and_3_out, and_4_out, and_5_out, and_6_out, and_7_out, and_8_out, and_9_out,
       and_10_out, and_11_out, and_12_out, and_13_out, and_14_out, and_15_out, and_16_out, and_17_out,
       and_18_out, and_19_out, and_20_out, and_21_out, and_23_out, and_24_out, and_25_out, and_26_out,
       and_27_out, and_28_out, and_29_out, and_30_out, and_31_out, and_32_out, and_33_out, and_34_out,
       and_35_out, and_36_out, and_37_out, and_38_out, and_39_out, and_40_out, and_41_out, and_42_out,
       and_43_out, and_44_out, and_45_out, and_46_out, and_47_out, and_48_out, and_49_out, and_50_out,
       and_51_out, and_52_out, and_53_out, and_54_out, and_55_out, and_56_out, and_57_out, and_58_out,
       and_59_out, and_60_out, and_61_out, and_62_out, and_63_out, buffer_1_out, buffer_2_out, nand_1_out,
       nand_2_out, nand_3_out, nand_4_out, nand_6_out, nand_7_out, nand_8_out, nand_9_out, nand_10_out,
       nand_11_out, nand_12_out, nand_13_out, nand_14_out, nand_15_out, nand_16_out, nand_17_out,
       nand_18_out, nand_19_out, nand_20_out, nand_21_out, nand_22_out, nand_23_out, nand_24_out,
       nand_25_out, nand_26_out, nand_27_out, nand_28_out, nand_29_out, nand_31_out, nand_33_out,
       nand_35_out, nand_37_out, nand_39_out, nand_40_out, nand_41_out, nand_42_out, nand_43_out,
       nand_44_out, nand_45_out, nand_46_out, nand_47_out, nand_48_out, nand_49_out, nand_50_out,
       nand_51_out, nand_52_out, nand_53_out, nand_54_out, nand_55_out, nand_56_out, nand_57_out,
       nand_58_out, nand_59_out, nand_60_out, nand_61_out, nand_62_out, nand_63_out, nand_64_out,
       nand_65_out, nand_66_out, nand_67_out, nand_68_out, nand_69_out, nand_70_out, nand_71_out,
       nand_72_out, nand_73_out, nand_74_out, nand_75_out, nand_76_out, nand_77_out, nand_78_out,
       nand_79_out, nand_80_out, nand_81_out, nand_82_out, nand_83_out, nand_84_out, nand_85_out,
       nand_86_out, nand_87_out, nand_88_out, nand_89_out, nand_90_out, nand_91_out, nand_93_out,
       nand_95_out, nand_97_out, nand_99_out, nand_101_out, nand_103_out, nand_105_out, nand_107_out,
       nand_108_out, nand_109_out, nand_110_out, nand_111_out, nand_112_out, nand_113_out, nand_114_out,
       nand_115_out, nand_116_out, nand_117_out, nand_118_out, nand_119_out, nand_120_out, nand_121_out,
       nand_122_out, nand_123_out, nand_124_out, nand_125_out, nand_126_out, nand_127_out, nand_128_out,
       nand_129_out, nand_130_out, nand_131_out, nand_132_out, nand_133_out, nand_134_out, nand_135_out,
       nand_136_out, nand_137_out, nand_138_out, nand_139_out, nand_141_out, nand_143_out, nand_145_out,
       nand_147_out, nand_149_out, nand_151_out, nand_153_out, nand_155_out, nor_1_out, nor_2_out, nor_3_out,
       nor_4_out, not_1_out, not_2_out, not_3_out, not_4_out, not_5_out, not_6_out, not_7_out, not_8_out,
       not_9_out, not_10_out, not_11_out, not_12_out, not_13_out, not_14_out, not_15_out, not_16_out,
       not_17_out, not_18_out, not_19_out, not_20_out, not_21_out, not_22_out, not_23_out, not_24_out,
       not_25_out, not_26_out, not_27_out, not_28_out, not_29_out, not_30_out, not_31_out, not_32_out,
       not_33_out, or_1_out, or_2_out, or_3_out, or_4_out, or_5_out, or_6_out, or_7_out, or_8_out, or_9_out,
       or_10_out, or_11_out, or_12_out, or_13_out, or_14_out, or_15_out, or_16_out, or_17_out, or_18_out,
       undriven, undriven_2, undriven_3, undriven_4, undriven_5, undriven_6, undriven_7, undriven_8,
       undriven_9, undriven_10, undriven_11, undriven_12, undriven_13, undriven_14, undriven_15, undriven_16,
       undriven_17, undriven_18, undriven_19, undriven_20, undriven_21, undriven_22, undriven_23,
       undriven_24, undriven_25, undriven_26, undriven_27, undriven_28, undriven_29, undriven_30,
       undriven_31, undriven_32, xnor_1_out, xnor_2_out, xnor_3_out, xnor_4_out, xor_1_out, xor_2_out,
       xor_3_out, xor_4_out;

  not not_1 (not_1_out, nE1);
  not not_2 (not_2_out, B);
  not not_3 (not_3_out, A);
  not not_4 (not_4_out, nE2);
  not not_5 (not_5_out, not_2_out);
  not not_6 (not_6_out, not_3_out);
  nand nand_1 (nand_1_out, nand_3_out, nand_2_out);
  nand nand_2 (nand_2_out, D, nCLR_2, nand_4_out);
  buf buffer_1 (buffer_1_out, nCLR_3);
  not not_7 (not_7_out, nLOAD);
  and and_1 (and_1_out, nLOAD, ENP, ENT);
  not not_8 (not_8_out, not_7_out);
  and and_2 (and_2_out, not_7_out, DATA_A);
  and and_3 (and_3_out, not_7_out, DATA_B);
  and and_4 (and_4_out, not_7_out, DATA_C);
  and and_5 (and_5_out, not_7_out, DATA_C_2);
  and and_6 (and_6_out, not_1_out, not_2_out, not_3_out, _1C0);
  and and_7 (and_7_out, not_1_out, not_2_out, not_6_out, _1C1);
  and and_8 (and_8_out, not_1_out, not_5_out, not_3_out, _1C2);
  and and_9 (and_9_out, not_1_out, not_5_out, not_6_out, _1C3);
  and and_10 (and_10_out, _2C0, not_2_out, not_3_out, not_4_out);
  and and_11 (and_11_out, _2C1, not_2_out, not_6_out, not_4_out);
  and and_12 (and_12_out, _2C2, not_5_out, not_3_out, not_4_out);
  and and_13 (and_13_out, _2C3, not_5_out, not_6_out, not_4_out);
  nand nand_3 (nand_3_out, nand_1_out, CLK_3, nCLR_2);
  nand nand_4 (nand_4_out, nand_3_out, CLK_3, nand_2_out);
  not not_9 (not_9_out, and_1_out);
  not not_10 (not_10_out, nand_31_out);
  not not_11 (not_11_out, nand_33_out);
  not not_12 (not_12_out, nand_35_out);
  or or_1 (or_1_out, and_6_out, and_7_out, and_8_out, and_9_out);
  or or_2 (or_2_out, and_10_out, and_11_out, and_12_out, and_13_out);
  nand nand_5 (Q, nand_3_out, nand_6_out);
  nand nand_6 (nand_6_out, Q, nCLR_2, nand_4_out);
  and and_14 (and_14_out, QA_2, not_8_out, not_9_out);
  and and_15 (and_15_out, and_1_out, nand_31_out);
  nand nand_7 (nand_7_out, not_10_out, and_1_out);
  and and_16 (and_16_out, QB, nand_7_out, not_8_out);
  and and_17 (and_17_out, not_10_out, and_1_out, nand_33_out);
  nand nand_8 (nand_8_out, not_11_out, not_10_out, and_1_out);
  and and_18 (and_18_out, QC, nand_8_out, not_8_out);
  and and_19 (and_19_out, not_11_out, not_10_out, and_1_out, nand_35_out);
  and and_20 (and_20_out, QD, nand_9_out, not_8_out);
  nand nand_9 (nand_9_out, not_12_out, not_10_out, not_11_out, and_1_out);
  and and_21 (and_21_out, not_12_out, not_11_out, not_10_out, and_1_out, nand_37_out);
  not not_13 (not_13_out, nand_37_out);
  LED led_1 (.in(or_1_out));
  LED led_2 (.in(or_2_out));
  or or_3 (or_3_out, and_14_out, and_15_out, and_2_out);
  or or_4 (or_4_out, and_16_out, and_17_out, and_3_out);
  or or_5 (or_5_out, and_18_out, and_19_out, and_4_out);
  or or_6 (or_6_out, and_20_out, and_21_out, and_5_out);
  nand nand_10 (nand_10_out, nand_20_out, nand_11_out);
  nand nand_11 (nand_11_out, or_3_out, buffer_1_out, nand_21_out);
  nand nand_12 (nand_12_out, nand_22_out, nand_13_out);
  nand nand_13 (nand_13_out, or_4_out, buffer_1_out, nand_23_out);
  nand nand_14 (nand_14_out, nand_24_out, nand_15_out);
  nand nand_15 (nand_15_out, buffer_1_out, or_5_out, nand_25_out);
  nand nand_16 (nand_16_out, nand_26_out, nand_17_out);
  nand nand_17 (nand_17_out, buffer_1_out, or_6_out, nand_27_out);
  and and_22 (RCO, not_13_out, not_12_out, not_11_out, not_10_out, ENT);
  not not_14 (not_14_out, undriven);
  nand nand_18 (nand_18_out, nand_28_out, nand_19_out);
  nand nand_19 (nand_19_out, D_2, nand_29_out);
  nand nand_20 (nand_20_out, nand_10_out, CLK_5, buffer_1_out);
  nand nand_21 (nand_21_out, nand_20_out, CLK_5, nand_11_out);
  nand nand_22 (nand_22_out, nand_12_out, CLK_5, buffer_1_out);
  nand nand_23 (nand_23_out, nand_22_out, CLK_5, nand_13_out);
  nand nand_24 (nand_24_out, nand_14_out, CLK_5, buffer_1_out);
  nand nand_25 (nand_25_out, nand_24_out, CLK_5, nand_15_out);
  nand nand_26 (nand_26_out, nand_16_out, CLK_5, buffer_1_out);
  nand nand_27 (nand_27_out, nand_26_out, CLK_5, nand_17_out);
  and and_23 (and_23_out, ~not_14_out, ~undriven_2);  // AND_Gate
  and and_24 (and_24_out, ~undriven, ~undriven_2);  // AND_Gate
  nand nand_28 (nand_28_out, nand_18_out, CLK_4);
  nand nand_29 (nand_29_out, nand_28_out, CLK_4, nand_19_out);
  nand nand_30 (QA_2, nand_20_out, nand_31_out);
  nand nand_31 (nand_31_out, QA_2, buffer_1_out, nand_21_out);
  nand nand_32 (QB, nand_22_out, nand_33_out);
  nand nand_33 (nand_33_out, QB, buffer_1_out, nand_23_out);
  nand nand_34 (QC, nand_24_out, nand_35_out);
  nand nand_35 (nand_35_out, QC, buffer_1_out, nand_25_out);
  nand nand_36 (QD, nand_26_out, nand_37_out);
  nand nand_37 (nand_37_out, QD, buffer_1_out, nand_27_out);
  and and_25 (and_25_out, and_23_out, undriven_3);
  and and_26 (and_26_out, and_24_out, undriven_4);
  and and_27 (and_27_out, and_23_out, undriven_5);
  and and_28 (and_28_out, and_24_out, undriven_6);
  and and_29 (and_29_out, and_23_out, undriven_7);
  and and_30 (and_30_out, and_24_out, undriven_8);
  and and_31 (and_31_out, and_23_out, undriven_9);
  and and_32 (and_32_out, and_24_out, undriven_10);
  nand nand_38 (QA, nand_28_out, nand_39_out);
  nand nand_39 (nand_39_out, QA, nand_29_out);
  or or_7 (or_7_out, and_25_out, and_26_out);
  or or_8 (or_8_out, and_27_out, and_28_out);
  or or_9 (or_9_out, and_29_out, and_30_out);
  or or_10 (or_10_out, and_31_out, and_32_out);
  nand nand_40 (nand_40_out, undriven_11, undriven_12);
  xnor xnor_1 (xnor_1_out, undriven_11, undriven_12);
  nand nand_41 (nand_41_out, undriven_13, undriven_14);
  xnor xnor_2 (xnor_2_out, undriven_13, undriven_14);
  nand nand_42 (nand_42_out, undriven_15, undriven_19);
  xnor xnor_3 (xnor_3_out, undriven_15, undriven_19);
  nand nand_43 (nand_43_out, undriven_16, undriven_17);
  xnor xnor_4 (xnor_4_out, undriven_16, undriven_17);
  not not_15 (not_15_out, undriven_18);
  and and_33 (and_33_out, xnor_2_out, nand_40_out);
  and and_34 (and_34_out, xnor_3_out, nand_40_out, nand_41_out);
  and and_35 (and_35_out, xnor_4_out, nand_40_out, nand_41_out, nand_42_out);
  and and_36 (and_36_out, nand_40_out, nand_41_out, nand_42_out, nand_43_out, not_15_out);
  and and_37 (and_37_out, nand_40_out, ~xnor_1_out);  // AND_Gate
  buf and_38 (and_38_out, xnor_3_out);  // AND_Gate
  buf and_39 (and_39_out, xnor_4_out);  // AND_Gate
  buf and_40 (and_40_out, not_15_out);  // AND_Gate
  and and_41 (and_41_out, nand_41_out, ~xnor_2_out);  // AND_Gate
  and and_42 (and_42_out, xnor_4_out, nand_42_out);
  and and_43 (and_43_out, nand_42_out, nand_43_out, not_15_out);
  and and_44 (and_44_out, nand_42_out, ~xnor_3_out);  // AND_Gate
  and and_45 (and_45_out, nand_43_out, not_15_out);
  and and_46 (and_46_out, nand_43_out, ~xnor_4_out);  // AND_Gate
  not not_16 (not_16_out, not_15_out);
  nor nor_1 (nor_1_out, xnor_1_out, and_33_out, and_34_out, and_35_out, and_36_out);
  nor nor_2 (nor_2_out, xnor_2_out, and_38_out, and_39_out, and_40_out);
  nor nor_3 (nor_3_out, xnor_3_out, and_42_out, and_43_out);
  nor nor_4 (nor_4_out, xnor_4_out, and_45_out);
  xor xor_1 (xor_1_out, and_37_out, nor_2_out);
  xor xor_2 (xor_2_out, and_41_out, nor_3_out);
  xor xor_3 (xor_3_out, and_44_out, nor_4_out);
  xor xor_4 (xor_4_out, and_46_out, not_16_out);
  and and_47 (and_47_out, undriven_20, ~undriven_21, ~undriven_22);  // AND_Gate
  not not_17 (not_17_out, undriven_23);
  not not_18 (not_18_out, undriven_24);
  not not_19 (not_19_out, undriven_25);
  not not_20 (not_20_out, not_17_out);
  not not_21 (not_21_out, not_18_out);
  not not_22 (not_22_out, not_19_out);
  nand nand_44 (nand_44_out, undriven_26, not_17_out, not_19_out, and_47_out);
  nand nand_45 (nand_45_out, not_20_out, not_17_out, not_19_out, and_47_out);
  nand nand_46 (nand_46_out, undriven_26, not_21_out, not_19_out, and_47_out);
  nand nand_47 (nand_47_out, not_20_out, not_21_out, not_19_out, and_47_out);
  nand nand_48 (nand_48_out, undriven_26, not_17_out, not_22_out, and_47_out);
  nand nand_49 (nand_49_out, not_17_out, not_22_out, not_20_out, and_47_out);
  nand nand_50 (nand_50_out, undriven_26, not_22_out, not_21_out, and_47_out);
  nand nand_51 (nand_51_out, and_47_out, not_21_out, not_20_out, not_22_out);
  not not_23 (not_23_out, undriven_27);
  not not_24 (not_24_out, undriven_28);
  not not_25 (not_25_out, undriven_29);
  not not_26 (not_26_out, undriven_30);
  not not_27 (not_27_out, undriven_31);
  not not_28 (not_28_out, undriven_32);
  not not_29 (not_29_out, not_23_out);
  not not_30 (not_30_out, not_24_out);
  not not_31 (not_31_out, not_26_out);
  not not_32 (not_32_out, not_27_out);
  nand nand_52 (nand_52_out, not_29_out, not_30_out, not_25_out);
  nand nand_53 (nand_53_out, not_30_out, not_24_out, not_25_out);
  nand nand_54 (nand_54_out, not_30_out, not_23_out, not_25_out);
  nand nand_55 (nand_55_out, not_25_out, not_23_out, not_24_out);
  nand nand_56 (nand_56_out, not_31_out, not_32_out, not_28_out);
  nand nand_57 (nand_57_out, not_32_out, not_27_out, not_28_out);
  nand nand_58 (nand_58_out, not_32_out, not_26_out, not_28_out);
  nand nand_59 (nand_59_out, not_28_out, not_26_out, not_27_out);
  not not_33 (not_33_out, nENABLE);
  and and_48 (and_48_out, Q0_2, ~not_33_out);  // AND_Gate
  and and_49 (and_49_out, D0_2, not_33_out);
  and and_50 (and_50_out, Q1_2, ~not_33_out);  // AND_Gate
  and and_51 (and_51_out, D1_2, not_33_out);
  and and_52 (and_52_out, Q2_2, ~not_33_out);  // AND_Gate
  and and_53 (and_53_out, D2_2, not_33_out);
  and and_54 (and_54_out, Q3_2, ~not_33_out);  // AND_Gate
  and and_55 (and_55_out, D3_2, not_33_out);
  and and_56 (and_56_out, Q4_2, ~not_33_out);  // AND_Gate
  and and_57 (and_57_out, D4_2, not_33_out);
  and and_58 (and_58_out, Q5_2, ~not_33_out);  // AND_Gate
  and and_59 (and_59_out, D5_2, not_33_out);
  and and_60 (and_60_out, Q6_2, ~not_33_out);  // AND_Gate
  and and_61 (and_61_out, D6_2, not_33_out);
  and and_62 (and_62_out, Q7_2, ~not_33_out);  // AND_Gate
  and and_63 (and_63_out, D7_2, not_33_out);
  or or_11 (or_11_out, and_48_out, and_49_out);
  or or_12 (or_12_out, and_50_out, and_51_out);
  or or_13 (or_13_out, and_52_out, and_53_out);
  or or_14 (or_14_out, and_54_out, and_55_out);
  or or_15 (or_15_out, and_56_out, and_57_out);
  or or_16 (or_16_out, and_58_out, and_59_out);
  or or_17 (or_17_out, and_60_out, and_61_out);
  or or_18 (or_18_out, and_62_out, and_63_out);
  nand nand_60 (nand_60_out, nand_76_out, nand_61_out);
  nand nand_61 (nand_61_out, or_11_out, nand_77_out);
  nand nand_62 (nand_62_out, nand_78_out, nand_63_out);
  nand nand_63 (nand_63_out, or_12_out, nand_79_out);
  nand nand_64 (nand_64_out, nand_80_out, nand_65_out);
  nand nand_65 (nand_65_out, or_13_out, nand_81_out);
  nand nand_66 (nand_66_out, nand_82_out, nand_67_out);
  nand nand_67 (nand_67_out, or_14_out, nand_83_out);
  nand nand_68 (nand_68_out, nand_84_out, nand_69_out);
  nand nand_69 (nand_69_out, or_15_out, nand_85_out);
  nand nand_70 (nand_70_out, nand_86_out, nand_71_out);
  nand nand_71 (nand_71_out, or_16_out, nand_87_out);
  nand nand_72 (nand_72_out, nand_88_out, nand_73_out);
  nand nand_73 (nand_73_out, or_17_out, nand_89_out);
  nand nand_74 (nand_74_out, nand_90_out, nand_75_out);
  nand nand_75 (nand_75_out, or_18_out, nand_91_out);
  nand nand_76 (nand_76_out, nand_60_out, CLK_2);
  nand nand_77 (nand_77_out, nand_76_out, CLK_2, nand_61_out);
  nand nand_78 (nand_78_out, nand_62_out, CLK_2);
  nand nand_79 (nand_79_out, nand_78_out, CLK_2, nand_63_out);
  nand nand_80 (nand_80_out, nand_64_out, CLK_2);
  nand nand_81 (nand_81_out, nand_80_out, CLK_2, nand_65_out);
  nand nand_82 (nand_82_out, nand_66_out, CLK_2);
  nand nand_83 (nand_83_out, nand_82_out, CLK_2, nand_67_out);
  nand nand_84 (nand_84_out, nand_68_out, CLK_2);
  nand nand_85 (nand_85_out, nand_84_out, CLK_2, nand_69_out);
  nand nand_86 (nand_86_out, nand_70_out, CLK_2);
  nand nand_87 (nand_87_out, nand_86_out, CLK_2, nand_71_out);
  nand nand_88 (nand_88_out, nand_72_out, CLK_2);
  nand nand_89 (nand_89_out, nand_88_out, CLK_2, nand_73_out);
  nand nand_90 (nand_90_out, nand_74_out, CLK_2);
  nand nand_91 (nand_91_out, nand_90_out, CLK_2, nand_75_out);
  nand nand_92 (Q0_2, nand_76_out, nand_93_out);
  nand nand_93 (nand_93_out, Q0_2, nand_77_out);
  nand nand_94 (Q1_2, nand_78_out, nand_95_out);
  nand nand_95 (nand_95_out, Q1_2, nand_79_out);
  nand nand_96 (Q2_2, nand_80_out, nand_97_out);
  nand nand_97 (nand_97_out, Q2_2, nand_81_out);
  nand nand_98 (Q3_2, nand_82_out, nand_99_out);
  nand nand_99 (nand_99_out, Q3_2, nand_83_out);
  nand nand_100 (Q4_2, nand_84_out, nand_101_out);
  nand nand_101 (nand_101_out, Q4_2, nand_85_out);
  nand nand_102 (Q5_2, nand_86_out, nand_103_out);
  nand nand_103 (nand_103_out, Q5_2, nand_87_out);
  nand nand_104 (Q6_2, nand_88_out, nand_105_out);
  nand nand_105 (nand_105_out, Q6_2, nand_89_out);
  nand nand_106 (Q7_2, nand_90_out, nand_107_out);
  nand nand_107 (nand_107_out, Q7_2, nand_91_out);
  buf buffer_2 (buffer_2_out, nCLR);
  nand nand_108 (nand_108_out, nand_124_out, nand_109_out);
  nand nand_109 (nand_109_out, D0, buffer_2_out, nand_125_out);
  nand nand_110 (nand_110_out, nand_126_out, nand_111_out);
  nand nand_111 (nand_111_out, D1, buffer_2_out, nand_127_out);
  nand nand_112 (nand_112_out, nand_128_out, nand_113_out);
  nand nand_113 (nand_113_out, D2, buffer_2_out, nand_129_out);
  nand nand_114 (nand_114_out, nand_130_out, nand_115_out);
  nand nand_115 (nand_115_out, D3, buffer_2_out, nand_131_out);
  nand nand_116 (nand_116_out, nand_132_out, nand_117_out);
  nand nand_117 (nand_117_out, D4, buffer_2_out, nand_133_out);
  nand nand_118 (nand_118_out, nand_134_out, nand_119_out);
  nand nand_119 (nand_119_out, D5, buffer_2_out, nand_135_out);
  nand nand_120 (nand_120_out, nand_136_out, nand_121_out);
  nand nand_121 (nand_121_out, D6, buffer_2_out, nand_137_out);
  nand nand_122 (nand_122_out, nand_138_out, nand_123_out);
  nand nand_123 (nand_123_out, D7, buffer_2_out, nand_139_out);
  nand nand_124 (nand_124_out, nand_108_out, CLK, buffer_2_out);
  nand nand_125 (nand_125_out, nand_124_out, CLK, nand_109_out);
  nand nand_126 (nand_126_out, nand_110_out, CLK, buffer_2_out);
  nand nand_127 (nand_127_out, nand_126_out, CLK, nand_111_out);
  nand nand_128 (nand_128_out, nand_112_out, CLK, buffer_2_out);
  nand nand_129 (nand_129_out, nand_128_out, CLK, nand_113_out);
  nand nand_130 (nand_130_out, nand_114_out, CLK, buffer_2_out);
  nand nand_131 (nand_131_out, nand_130_out, CLK, nand_115_out);
  nand nand_132 (nand_132_out, nand_116_out, CLK, buffer_2_out);
  nand nand_133 (nand_133_out, nand_132_out, CLK, nand_117_out);
  nand nand_134 (nand_134_out, nand_118_out, CLK, buffer_2_out);
  nand nand_135 (nand_135_out, nand_134_out, CLK, nand_119_out);
  nand nand_136 (nand_136_out, nand_120_out, CLK, buffer_2_out);
  nand nand_137 (nand_137_out, nand_136_out, CLK, nand_121_out);
  nand nand_138 (nand_138_out, nand_122_out, CLK, buffer_2_out);
  nand nand_139 (nand_139_out, nand_138_out, CLK, nand_123_out);
  nand nand_140 (Q0, nand_124_out, nand_141_out);
  nand nand_141 (nand_141_out, Q0, buffer_2_out, nand_125_out);
  nand nand_142 (Q1, nand_126_out, nand_143_out);
  nand nand_143 (nand_143_out, Q1, buffer_2_out, nand_127_out);
  nand nand_144 (Q2, nand_128_out, nand_145_out);
  nand nand_145 (nand_145_out, Q2, buffer_2_out, nand_129_out);
  nand nand_146 (Q3, nand_130_out, nand_147_out);
  nand nand_147 (nand_147_out, Q3, buffer_2_out, nand_131_out);
  nand nand_148 (Q4, nand_132_out, nand_149_out);
  nand nand_149 (nand_149_out, Q4, buffer_2_out, nand_133_out);
  nand nand_150 (Q5, nand_134_out, nand_151_out);
  nand nand_151 (nand_151_out, Q5, buffer_2_out, nand_135_out);
  nand nand_152 (Q6, nand_136_out, nand_153_out);
  nand nand_153 (nand_153_out, Q6, buffer_2_out, nand_137_out);
  nand nand_154 (Q7, nand_138_out, nand_155_out);
  nand nand_155 (nand_155_out, Q7, buffer_2_out, nand_139_out);

  // Notes on the sheet:
  //   74xx153 Dual 4-to-1 Multiplexer
  //   Edge triggered D flip-flop with clear
  //   Y1
  //   Y2
  //   74xx161 4-Bit Counter
  //   S
  //   /E
  //   I1d
  //   I0d
  //   I1c
  //   I0c
  //   I1b
  //   I0b
  //   I1a
  //   I0a
  //   74xx157 Quad 2-to-1 Multiplexer
  //   Edge triggered D flip-flop
  //   Zd
  //   Zc
  //   Zb
  //   Za
  //   B4
  //   A4
  //   B3
  //   A3
  //   B2
  //   A2
  //   B1
  //   A1
  //   C0
  //   74xx283 4-Bit Adder
  //   C4
  //   S3
  //   S2
  //   S1
  //   S0
  //   E3
  //   /E2
  //   /E1
  //   A0
  //   A1
  //   A2
  //   74xx138 3-to-8 Decoder
  //   /O0
  //   /O1
  //   /O2
  //   /O3
  //   /O4
  //   /O5
  //   /O6
  //   /O7
  //   A1
  //   A0
  //   /E
  //   A1
  //   A0
  //   /E
  //   74xx139 Dual 2-to-4 Decoder
  //   /O0
  //   /O1
  //   /O2
  //   /O3
  //   /O0
  //   /O1
  //   /O2
  //   /O3
  //   74xx377 Octal D-type Flip-Flops with Common Enable
  //   74xxx273 8-Bit D-type Register
  //   RCO
endmodule
